// Logisim project mux_gate.circ as structural Verilog: 1 circuit, main circuit main
module main (
  input  a,
  input  sel,
  input  b,
  output out_4
);

  wire AND_2_out, AND_out, not_1_out;

  and AND (AND_out, a, not_1_out);
  not not_1 (not_1_out, sel);
  and AND_2 (AND_2_out, sel, b);
  or OR (out_4, AND_out, AND_2_out);
endmodule
