// Logisim project 1bitregister_test_bench.circ as structural Verilog: 1 circuit, main circuit main
module main (
  input  in_1,
  input  in_2,
  input  in_3,
  input  in_4,
  input  load,
  input  in_6,
  input  in,
  input  in_8,
  input  load_2,
  input  in_10,
  input  in_5,
  input  in_12,
  input  in_13,
  input  in_14,
  input  in_15,
  input  in_16,
  output out_17,
  output out_18,
  output out_19,
  output out_20,
  output out_21,
  output out_22,
  output out_23
);

  wire clock_1_out, d_ff_1_q, d_ff_1_qn, multiplexer_2_out, multiplexer_3_out;

  Multiplexer #(.enable("false")) multiplexer_1 (.in0(in_1), .in1(in_2), .out(out_17), .sel(in_4));
  Clock clock_1 (.out(clock_1_out));
  Multiplexer #(.enable("false")) multiplexer_2 (.in0(out_21), .in1(in_5), .out(multiplexer_2_out), .sel(load_2));
  D_Flip_Flop #(.trigger("low")) d_ff_1 (
    .D(multiplexer_3_out), .Q(d_ff_1_q), .Qn(d_ff_1_qn), .preset(load));  // open: clk, en, reset
  Multiplexer #(.enable("false")) multiplexer_3 (.in0(in), .out(multiplexer_3_out), .sel(load));  // open: in1
  D_Flip_Flop #(.trigger("low")) d_ff_2 (
    .clk(clock_1_out), .D(multiplexer_2_out), .Q(out_21), .Qn(out_22), .preset(in_12), .en(in_13),
    .reset(in_14));
  nor nor_1 (out_18, in_3, out_19);
  nor nor_2 (out_19, out_18, in_6);
  nor nor_3 (out_20, in_8, in_10);
  nand nand_1 (out_23, in_15, in_16);
endmodule
